# Fritzing sketch cooler (saved by Fritzing 0.9.3b)
breadboards: 1

parts:
  DS1 = DS18B20 1-Wire Temperature Sensor [part_number=DS18B20]
  External_Pullup = Resistor [tolerance=±5% resistance=4.7k package="0603 [SMD]"]
  FAN = Basic Servo
  U1 = ATMEGA32U4 [package=qfn]

nets:
  GND/Supply GND: DS1.GND, FAN.gnd, U1.GND
  Pin 7: DS1.DQ, External_Pullup.Pin_0, U1.PE6
  VDD: DS1.VDD, External_Pullup.Pin_1, U1.VCC
  24V: FAN.vcc
  Pin 6: FAN.pulse, U1.PD7(ADC10)
